// Logisim project CPU.circ as structural Verilog
module OneBitAdder (
  input  A,
  input  B,
  input  C_in,
  output Sum,
  output C_out
);

  wire not_1_out, not_2_out, or_1_out, or_2_out, xor_1_out;

  xor xor_1 (xor_1_out, B, C_in);
  xor xor_2 (Sum, A, xor_1_out);
  not not_1 (not_1_out, Sum);
  not not_2 (not_2_out, xor_1_out);
  or or_1 (or_1_out, not_1_out, not_2_out);
  or or_2 (or_2_out, B, C_in);
  and and_1 (C_out, or_1_out, or_2_out);
endmodule

module FourBitAdder (
  input  A3,
  input  A2,
  input  A1,
  input  A0,
  input  B3,
  input  B2,
  input  B1,
  input  B0,
  output O,
  output X3,
  output X2,
  output X1,
  output X0
);

  wire onebitadder_2_c_out, onebitadder_3_c_out, onebitadder_4_c_out;

  OneBitAdder onebitadder_1 (.A(A3), .B(B3), .C_in(onebitadder_2_c_out), .Sum(X3), .C_out(O));
  OneBitAdder onebitadder_2 (.A(A2), .B(B2), .C_in(onebitadder_3_c_out), .Sum(X2), .C_out(onebitadder_2_c_out));
  OneBitAdder onebitadder_3 (.A(A1), .B(B1), .C_in(onebitadder_4_c_out), .Sum(X1), .C_out(onebitadder_3_c_out));
  OneBitAdder onebitadder_4 (.A(A0), .B(B0), .Sum(X0), .C_out(onebitadder_4_c_out));  // open: C_in
endmodule

module FourBitInverter (
  input  A3,
  input  A2,
  input  A1,
  input  A0,
  output Y3,
  output Y2,
  output Y1,
  output Y0
);

  not not_1 (Y3, A3);
  not not_2 (Y2, A2);
  not not_3 (Y1, A1);
  not not_4 (Y0, A0);
endmodule
